# Fritzing sketch Biometric_Panic_Box (saved by Fritzing 0.8.7b)
breadboards: 1

parts:
  Part1 = Arduino Uno (Rev3)
  LED1 = LED - 3mm [color="Red (633nm)" package="3 mm [THT]"]
  S2 = Round Pushbutton
  S3 = Round Pushbutton
  S4 = Round Pushbutton
  U1 = LCD-16X2 [package=lcd-16x2]
  U2 = ESP8266 WiFi Module [part_number=ESP8266]
  Raspberry_Pi_1 = Raspberry Pi 3  # not connected
  Mod1 = sensor_biometrico
  U3 = POT [package=pot_alpha_rv16af-20]
  R1 = Resistor [tolerance=±5% resistance=220 package=THT]
  R2 = Resistor [tolerance=±5% resistance=220 package=THT]
  R3 = Resistor [package="2010 [SMD]"]
  R4 = Resistor [package="2010 [SMD]"]
  R5 = Resistor [package="2010 [SMD]"]

nets:
  N1: Part1.A0, S3.leg0, R5.Pin_0
  N2: Part1.A1, S4.leg0, R4.Pin_0
  N3: Part1.A2, S2.leg0, R3.Pin_0
  N4: Part1.D8, LED1.anode, R2.Pin_0, R2.Pin_1
  N5: Part1.D10_PWM/SS, U2.TXD
  N6: Part1.D11_PWM/MOSI, U2.RXD
  N7: Part1.D12/MISO, Mod1.RX
  N8: Part1.D13/SCK, Mod1.TX
  N9: Part1.D2, U1.RS
  N10: Part1.D3_PWM, U1.E
  N11: Part1.D4, U1.DB4
  N12: Part1.D5_PWM, U1.DB5
  N13: Part1.D6_PWM, U1.DB6
  N14: Part1.D7, U1.DB7
  3V3: Part1.3V3, U2.VCC, U2.RST
  5V: Part1.5V, S2.leg1, S3.leg1, S4.leg1, U1.VDD, Mod1.VCC, U3.A, R1.Pin_0
  GND: Part1.GND, LED1.cathode, U1.VSS, U1.R_W, U1.K, U2.GND, Mod1.GND, U3.E, R3.Pin_1, R4.Pin_1, R5.Pin_1
  N15: U1.VO, U3.S
  N16: U1.A, R1.Pin_1

custom parts:
  ESP8266 WiFi Module: Generic WiFi Module based on the ESP8266 with onboard PCB antenna and UART communications
  sensor_biometrico: Adafruit Optical Fingerprint Sensor
